# Fritzing sketch gesture switch (saved by Fritzing 0.9.3b)
breadboards: 1

parts:
  Raspberry_Pi4 = Raspberry Pi 3 [part_number=RPI-3-V1.2]
  VL53L0_TOF_Sensor = Adafruit VL530X Time of Flight Distance Sensor [part_number="Adafruit #3317"]
  BUZZER = Piezo Speaker
  RGB_LED = RGB LED - (4 legs) [package="5 mm [THT]"]
  R1 = Resistor [tolerance=±5% resistance=220 package="1206 [SMD]"]
  R5 = Resistor [tolerance=±5% resistance=220 package="1206 [SMD]"]
  R6 = Resistor [tolerance=±5% resistance=220 package="1206 [SMD]"]

nets:
  3V3: Raspberry_Pi4.3v3, VL53L0_TOF_Sensor.VCC, RGB_LED.common_anode
  N1: Raspberry_Pi4.GPIO2, VL53L0_TOF_Sensor.SDA
  N2: Raspberry_Pi4.GPIO3, VL53L0_TOF_Sensor.SCL
  GND: Raspberry_Pi4.GND, VL53L0_TOF_Sensor.GND, BUZZER.pin1
  N3: Raspberry_Pi4.GIPO21, BUZZER.pin2
  N4: Raspberry_Pi4.GIPO18, R5.Pin_1
  N5: Raspberry_Pi4.GIPO15, R6.Pin_1
  N6: Raspberry_Pi4.GIPO14, R1.Pin_1
  N7: RGB_LED.red_cathode, R1.Pin_0
  N8: RGB_LED.green_cathode, R6.Pin_0
  N9: RGB_LED.blue_cathode, R5.Pin_0

custom parts:
  Adafruit VL530X Time of Flight Distance Sensor: The VL53L0X is a Time of Flight distance sensor like no other you've used! The sensor contains a very tiny invisible laser source, and a matching sensor. The VL53L0X can detect the "time of flight", or how long the light has taken to bounce back to the sensor. Since it uses a very narrow light source, it is good for determining distance of only the surface directly in front of it. Unlike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
